# Fritzing sketch wiring_w_volume_control (saved by Fritzing 0.9.3b)

parts:
  U1 = NodeMCU V3.0
  Bauteil1 = RFID-RC522-v2
  Bauteil2 = Adafruit PAM8302 [part_number="Adafruit #2130"]
  SP1 = SPEAKER [package=pcb_mount_speaker]
  VS1 = VS1053 [package=MP3]
  R1 = Rotary Potentiometer (Small) [maximum_resistance=1kΩ package=THT]

nets:
  N1: U1.D0, VS1.XDCS
  N2: U1.D1, VS1.DREQ
  N3: U1.D2, VS1.CS
  N4: U1.D3, VS1.XCS
  GND: U1.D4, U1.GND#6, U1.GND#13, U1.GND#33, Bauteil1.GND, Bauteil2.GND, Bauteil2.SD, Bauteil2.AIN-, R1.leg2
  3V3: U1.3V3, Bauteil1.3.3V, R1.leg1
  N5: U1.D5, Bauteil1.SCK, VS1.SCK
  N6: U1.D6, Bauteil1.MISO, VS1.MISO
  N7: U1.D7, Bauteil1.MOSI, VS1.MOSI
  N8: U1.D8, Bauteil1.SDA
  N9: U1.RST, VS1.XRESET
  VCC: U1.VU, Bauteil2.VCC, VS1.5V
  N10: U1.GND#41, VS1.GND
  N11: U1.A0, R1.wiper
  N12: Bauteil2.AIN+, VS1.Audio
  N13: Bauteil2.VO+, SP1.+
  N14: Bauteil2.VO-, SP1.-

custom parts:
  NodeMCU V3.0: ESP8266 based NodeMCU
  RFID-RC522-v2: A simple China made RFID-RC522 Reader; do check the pin labels, as this is a MFRC522 based clone.
  Adafruit PAM8302: This super small mono amplifier is surprisingly powerful - able to deliver up to 2.5 Watts into 4-8 ohm impedance speakers. Inside the miniature chip is a class D controller, able to run from 2.0V-5.5VDC. Since the amp is a class D, its very efficient (over 90% efficient when driving an 8Ω speaker at over half a Watt) - making it perfect for portable and battery-powered projects. It has built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
  VS1053: VS1053 Breakout Board
